# Fritzing sketch espeasy_esp_01 (saved by Fritzing 0.9.2b)
breadboards: 1

parts:
  Деталь1 = FTDI Basic Programmer
  U1 = ESP8266 WiFi Module [part_number=ESP8266]

nets:
  N1: Деталь1.RXI, U1.TXD
  N2: Деталь1.POWER, U1.VCC, U1.CH_PD
  GND: Деталь1.GND, U1.GND

custom parts:
  ESP8266 WiFi Module: Generic WiFi Module based on the ESP8266 with onboard PCB antenna and UART communications
