# Fritzing sketch Untitled Sketch (saved by Fritzing 0.9.2b)
breadboards: 1

parts:
  U1 = NodeMCU V1.0
  DS1 = DS18B20 1-Wire Temperature Sensor [part_number=DS18B20]
  R1 = Resistor [tolerance=±5% resistance=4.7 package="0805 [SMD]"]

nets:
  N1: U1.D4, DS1.DQ, R1.Pin_1
  3V3: U1.3V3, DS1.VDD, R1.Pin_0
  GND: U1.GND, DS1.GND

custom parts:
  NodeMCU V1.0: ESP9266 based NodeMCU
